# Fritzing sketch Untitled Sketch 2 (saved by Fritzing 0.9.3b)
breadboards: 1

parts:
  S1 = Pushbutton [package="[THT]"]
  S2 = Pushbutton [package="[THT]"]
  Part1 = Arduino Uno (Rev3)
  J1 = Piezo Speaker
  R1 = Resistor [tolerance=±5% resistance=330 package=THT]
  R2 = Resistor [tolerance=±5% resistance=9.1k package=THT]
  OLED1 = OLED 128x64 I2C Monochrome Display
  DHT1 = Humidity and Temperature Sensor DHT11
  R3 = Resistor [tolerance=±5% resistance=9.1k package=THT]

nets:
  N1: S1.Pin_1, S1.Pin_2, Part1.D10_PWM/SS, R2.Pin_0
  5V: S1.Pin_3, S1.Pin_4, S2.Pin_3, S2.Pin_4, Part1.5V, OLED1.VDD, DHT1.Vcc
  N2: S2.Pin_1, S2.Pin_2, Part1.D9_PWM, R3.Pin_0
  N3: Part1.A4/SDA, OLED1.SDA
  N4: Part1.A5/SCL, OLED1.SCK
  N5: Part1.D11_PWM/MOSI, R1.Pin_1
  N6: Part1.D2, DHT1.Data-signal
  GND: Part1.GND, J1.pin1, R2.Pin_1, OLED1.GND, DHT1.GND_1, R3.Pin_1
  N7: J1.pin2, R1.Pin_0

custom parts:
  Humidity and Temperature Sensor DHT11: Digital relative humidity & temperature sensor DHT11
